# Fritzing sketch circuit_python_tutorial_esp32 (saved by Fritzing 0.9.10b)
breadboards: 1

parts:
  Part2 = Adafruit BNO085 9-DOF Orientation IMU Fusion [part_number="Addfruit #4754"]
  Part3 = Adafruit ESP32-S3 Feather [part_number="Adafruit #5323"]

nets:
  VCC: Part2.VCC, Part2.PS1, Part3.3.3V
  GND: Part2.GND, Part3.GND, Part3.A2
  N1: Part2.SCL/SCK/RX, Part3.TX
  N2: Part2.SDA/MISO/TX, Part3.RX

custom parts:
  Adafruit ESP32-S3 Feather: The ESP32-S3 has arrived in Feather format - and what a great way to get started with this powerful new chip from Espressif! With dual 240 MHz cores, WiFi and BLE support, and native USB, this Feather is great for powering your IoT projects. That's right - it's the new Adafruit ESP32-S3 Feather! With native USB and 8 MB flash, this board will let you upgrade your existing ESP32 projects.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
