# Fritzing sketch circuit_python_tutorial_raspi (saved by Fritzing 0.9.10b)
breadboards: 1

parts:
  Raspberry_Pi_1 = Raspberry Pi 3 [part_number=RPI-3-V1.2]
  S4 = Pushbutton [package="[THT]"]
  LED1 = LED - 5mm [color="Red (633nm)" current=0.030 package="5 mm [THT]"]
  R1 = Resistor [tolerance=±5% power=0.25 resistance=220 package=THT]
  J1 = Basic Servo  # not connected

nets:
  N1: Raspberry_Pi_1.GIPO4, S4.Pin_3, S4.Pin_4
  N2: Raspberry_Pi_1.GND, S4.Pin_1, S4.Pin_2, R1.Pin_1
  N3: Raspberry_Pi_1.GIPO18, LED1.anode
  N4: LED1.cathode, R1.Pin_0
